# Fritzing sketch sketch (saved by Fritzing 1.0.4)
breadboards: 1

parts:
  U1 = XIAO ESP32C3
  SENSOR1 = Adafruit SHT4x [part_number="Adafruit #4885"]
  LCD1 = 1_54in tft lcd
  S1 = Pushbutton [package="[THT]"]
  BAT1 = Battery Holders [package=lipo-1100mAh]
  R1 = Resistor [tolerance=±5% power=0.25W resistance=1M package=THT]
  R2 = Resistor [tolerance=±5% power=0.25W resistance=1M package=THT]
  C1 = Ceramic Capacitor [capacitance=0.1nF voltage=35V package="100 mil [THT, multilayer]"]

nets:
  N1: U1.D0, LCD1.pin_8
  N2: U1.D1, LCD1.pin_7
  N3: U1.D2, R1.Pin_1, R2.Pin_0, C1.0
  N4: U1.D3, LCD1.pin_6
  N5: U1.D4, SENSOR1.SDA
  N6: U1.D5, SENSOR1.SCL
  N7: U1.D6, LCD1.pin_5
  N8: U1.D7, S1.Pin_3, S1.Pin_4
  N9: U1.D8, LCD1.pin3
  N10: U1.D10, LCD1.pin4
  N11: U1.3V3, LCD1.pin2
  GND: U1.GND, SENSOR1.GND, LCD1.pin_1, S1.Pin_1, S1.Pin_2
  5V: U1.5V, SENSOR1.VCC
  N12: BAT1.+, R2.Pin_1
  N13: BAT1.-, R1.Pin_0, C1.1

custom parts:
  XIAO ESP32C3: Seeed Studio XIAO ESP32C3 adopts new RISC-V architecture, supporting both Wi-Fi and BLE wireless connectivities. For Internet of Things applications, you will find it is flexible and suitable for all kinds of IoT scenarios.
  Adafruit SHT4x: Sensirion Temperature/Humidity sensors are some of the finest & highest-accuracy devices you can get. And finally, we have some that have a true I2C interface for easy reading. The SHT40 and SHT45 sensors are the fourth generation (started at the SHT10 and worked its way up to the top!). The SHT40 has an excellent ±1.8% typical relative humidity accuracy from 25 to 75% and ±0.2 °C typical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
  1_54in tft lcd: This is the DONGKER 1.54'' LCD Display Module, SPI 240x240 1.54'' LCD Display Module ST7789 Driver 240x240 3.3V IPS LCD Display Screen Module. The 1.54" display has 240x240 color pixels.
