# Fritzing sketch sketch_perfboard (saved by Fritzing 1.0.4)
circuit board: 8.08851cm x 5.68356cm
perfboards: 1

parts:
  S1 = Pushbutton [package="[THT]"]
  R1 = Resistor [tolerance=±5% power=0.25W resistance=1M package=THT]
  R2 = Resistor [tolerance=±5% power=0.25W resistance=1M package=THT]
  C1 = Ceramic Capacitor [capacitance=0.1nF voltage=35V package="100 mil [THT, multilayer]"]
  J1 = female pin header, 2 pins [form="♀ (female)" part_number=BAT]
  J2 = female pin header, 7 pins [form="♀ (female)" part_number=ESP32C3]
  J3 = female pin header, 7 pins [form="♀ (female)" part_number=ESP32C3]
  J4 = female pin header, 4 pins [form="♀ (female)" part_number=I2C]
  J5 = female pin header, 8 pins [form="♀ (female)" part_number=DISP]

nets:
  GND: S1.Pin_1, S1.Pin_2, J2.pin2, J4.pin2, J5.pin2
  D7: S1.Pin_3, S1.Pin_4, J2.pin7
  A2: R1.Pin_0, R2.Pin_0, C1.0, J3.pin3
  BAT -: R1.Pin_1, J1.pin1
  BAT+: R2.Pin_1, C1.1, J1.pin2
  V5V: J2.pin1, J4.pin1
  V3V3: J2.pin3, J5.pin1
  DIN/MOSI: J2.pin4, J5.pin3
  MISO: J2.pin5
  CLK/SCK: J2.pin6, J5.pin4
  BL/D0: J3.pin1, J5.pin8
  CS/D1: J3.pin2, J5.pin5
  D3/DS: J3.pin4, J5.pin6
  SDA: J3.pin5, J4.pin3
  SCL: J3.pin6, J4.pin4
  D6/RST: J3.pin7, J5.pin7
